// Logisim project NicholasALU.circ as structural Verilog: 5 circuits, main circuit main
module main (
  input  in_1,
  input  [3:0] in_2,
  input  [3:0] in_3,
  input  in_4,
  input  [1:0] OP,
  input  AINV,
  input  in_7,
  input  BINV,
  input  in_9
);

  wire A1, A2, A3, A4, AINV_t, ALU1, ALU2, ALU3, ALU4, and_2_out, B1, B2, B3, B4, BINV_t, CASE1, CASE2,
       CASE3, CASE4, clock_1_out, clock_2_out, clock_3_out, COUT1, COUT2, COUT3, not_1_out, not_2_out,
       not_3_out, not_4_out, not_5_out, not_6_out, not_7_out, not_8_out, not_9_out, not_10_out, not_11_out,
       not_12_out, not_13_out, or_1_out, OVERFLOW, ZERO;
  wire [0:0] xor_1_out;
  wire [1:0] OP_t;
  wire [2:0] register_6_q;
  wire [3:0] Result_q;

  Clock clock_1 (.out(clock_1_out));
  // Probe on in_2
  Register #(.width(4)) register_1 (.D(in_2), .clk(clock_1_out), .Q({A4, A3, A2, A1}));  // open: en, clr
  // Probe on in_3
  Register #(.width(4)) register_2 (.D(in_3), .clk(clock_1_out), .Q({B4, B3, B2, B1}));  // open: en, clr
  Register #(.width(2)) register_3 (.D(OP), .clk(clock_1_out), .Q(OP_t));  // open: en, clr
  Register #(.width(1)) register_4 (.D(AINV), .clk(clock_1_out), .Q(AINV_t));  // open: en, clr
  Register #(.width(1)) register_5 (.D(BINV), .clk(clock_1_out), .Q(BINV_t));  // open: en, clr
  BitALU bitalu_1 (
    .AINV(AINV_t), .OP(OP_t), .A1(A1), .BINV(BINV_t), .B1(B1), .CIN(BINV_t), .in_7(in_1), .O(ALU1),
    .COUT(COUT1));
  BitALU bitalu_2 (
    .AINV(AINV_t), .OP(OP_t), .A1(A2), .BINV(BINV_t), .B1(B2), .CIN(COUT1), .in_7(in_4), .O(ALU2),
    .COUT(COUT2));
  BitALU bitalu_3 (
    .AINV(AINV_t), .OP(OP_t), .A1(A3), .BINV(BINV_t), .B1(B3), .CIN(COUT2), .in_7(in_7), .O(ALU3),
    .COUT(COUT3));
  BitALU bitalu_4 (
    .AINV(AINV_t), .OP(OP_t), .A1(A4), .BINV(BINV_t), .B1(B4), .CIN(COUT3), .in_7(in_9), .O(ALU4));  // open: COUT
  not not_1 (not_1_out, ALU4);
  not not_2 (not_2_out, ALU3);
  not not_3 (not_3_out, ALU2);
  not not_4 (not_4_out, ALU1);
  and and_1 (ZERO, not_1_out, not_2_out, not_3_out, not_4_out);
  xor xor_1 (xor_1_out[0], ALU4, OVERFLOW);
  Register #(.width(4)) Result (.D({ALU4, ALU3, ALU2, ALU1}), .clk(clock_2_out), .Q(Result_q));  // open: en, clr
  Clock clock_2 (.out(clock_2_out));
  Clock clock_3 (.out(clock_3_out));
  or or_1 (or_1_out, CASE1, CASE2, CASE3, CASE4);
  not not_5 (not_5_out, OP_t[0]);
  and and_2 (and_2_out, not_5_out, OP_t[1]);
  // Probe on Result_q
  // Probe on Result_q
  Register #(.width(3)) register_6 (
    .D({OVERFLOW, ZERO, xor_1_out[0]}), .clk(clock_3_out), .Q(register_6_q));  // open: en, clr
  and and_3 (OVERFLOW, or_1_out, and_2_out);
  // Probe on register_6_q
  not not_6 (not_6_out, A4);
  not not_7 (not_7_out, B4);
  not not_8 (not_8_out, BINV_t);
  not not_9 (not_9_out, A4);
  and and_4 (CASE1, not_6_out, not_7_out, not_8_out, ALU4);
  and and_5 (CASE3, not_9_out, B4, BINV_t, ALU4);
  not not_10 (not_10_out, BINV_t);
  not not_11 (not_11_out, B4);
  and and_6 (CASE2, A4, B4, not_10_out, not_12_out);
  not not_12 (not_12_out, ALU4);
  and and_7 (CASE4, A4, not_11_out, BINV_t, not_13_out);
  not not_13 (not_13_out, ALU4);

  // Other names for the same wires on the sheet: C0 = BINV_t

  // Notes on the sheet:
  //   261101723
  //   A
  //   B
  //   NICHOLAS HAYEK
  //   INPUT REGISTERS
  //   Last input in ALU is typically SLT, but we set to 0 & don't use
  //   Status
  //   OF|Zero|Sign
  //   A > 0, B >0, A + B < 0
  //   A > 0, B < 0, A - B < 0
  //   Overflow Cases
  //   A < 0, B < 0, A + B> 0
  //   A < 0, B > 0, A - B > 0
endmodule

module BitALU (
  input  AINV,
  input  [1:0] OP,
  input  A1,
  input  BINV,
  input  B1,
  input  CIN,
  input  in_7,
  output O,
  output COUT
);

  wire and_1_out, bitmux_1_o, bitmux_2_o, fulladder_1_s, not_1_out, not_2_out, or_1_out;

  not not_1 (not_1_out, A1);
  not not_2 (not_2_out, B1);
  BitMUX bitmux_1 (.S(AINV), .IN1(A1), .IN2(not_1_out), .O(bitmux_1_o));
  BitMUX bitmux_2 (.S(BINV), .IN1(B1), .IN2(not_2_out), .O(bitmux_2_o));
  and and_1 (and_1_out, bitmux_1_o, bitmux_2_o);
  or or_1 (or_1_out, bitmux_1_o, bitmux_2_o);
  FullAdder fulladder_1 (.A(bitmux_1_o), .B(bitmux_2_o), .CIN(CIN), .S(fulladder_1_s), .COUT(COUT));
  HalfNibMUX halfnibmux_1 (.A0(and_1_out), .A1(or_1_out), .S(OP), .A2(fulladder_1_s), .A3(in_7), .O(O));
endmodule

module HalfNibMUX (
  input  A0,
  input  A1,
  input  [1:0] S,
  input  A2,
  input  A3,
  output O
);

  wire bitmux_1_o, bitmux_2_o;

  BitMUX bitmux_1 (.S(S[0]), .IN1(A0), .IN2(A1), .O(bitmux_1_o));
  BitMUX bitmux_2 (.S(S[0]), .IN1(A2), .IN2(A3), .O(bitmux_2_o));
  BitMUX bitmux_3 (.S(S[1]), .IN1(bitmux_1_o), .IN2(bitmux_2_o), .O(O));
endmodule

module FullAdder (
  input  A,
  input  B,
  input  CIN,
  output S,
  output COUT
);

  wire and_1_out, and_2_out, xor_1_out;

  xor xor_1 (xor_1_out, A, B);
  and and_1 (and_1_out, CIN, xor_1_out);
  and and_2 (and_2_out, B, A);
  xor xor_2 (S, xor_1_out, CIN);
  xor xor_3 (COUT, and_1_out, and_2_out);
endmodule

module BitMUX (
  input  S,
  input  IN1,
  input  IN2,
  output O
);

  wire and_1_out, and_2_out, not_1_out;

  not not_1 (not_1_out, S);
  and and_1 (and_1_out, IN1, not_1_out);
  and and_2 (and_2_out, S, IN2);
  or or_1 (O, and_1_out, and_2_out);
endmodule
