// Logisim project NicholasRAM.circ as structural Verilog: 5 circuits, main circuit main
module main (
  input  [1:0] ADDRESS,
  input  MODE,
  input  IN0,
  input  IN1,
  input  IN2,
  input  IN3,
  output OUT0,
  output OUT1,
  output OUT2,
  output OUT3
);

  wire and_1_out, and_2_out, and_3_out, and_4_out, clock_1_out, clock_2_out, clock_3_out, M,
       mydecoder_1_out0, mydecoder_1_out1, mydecoder_1_out2, mydecoder_1_out3, not_1_out;
  wire [1:0] A;
  wire [3:0] bigmux_1_o, nibblereg_1_q, nibblereg_2_q, nibblereg_3_q, nibblereg_4_q, nibblereg_5_q;

  not not_1 (not_1_out, M);
  MyDecoder mydecoder_1 (
    .S(A), .OUT0(mydecoder_1_out0), .OUT1(mydecoder_1_out1), .OUT2(mydecoder_1_out2), .OUT3(mydecoder_1_out3));
  and and_1 (and_1_out, mydecoder_1_out0, not_1_out);
  and and_2 (and_2_out, mydecoder_1_out1, not_1_out);
  and and_3 (and_3_out, mydecoder_1_out2, not_1_out);
  and and_4 (and_4_out, mydecoder_1_out3, not_1_out);
  Clock clock_1 (.out(clock_1_out));
  D_Flip_Flop d_ff_1 (.D(MODE), .clk(clock_2_out), .Q(M));  // open: Qn, preset, reset
  Clock clock_2 (.out(clock_2_out));
  NibbleReg nibblereg_1 (.D({IN3, IN2, IN1, IN0}), .C(and_1_out), .Q(nibblereg_1_q));
  NibbleReg nibblereg_2 (.D({IN3, IN2, IN1, IN0}), .C(and_2_out), .Q(nibblereg_2_q));
  NibbleReg nibblereg_3 (.D({IN3, IN2, IN1, IN0}), .C(and_3_out), .Q(nibblereg_3_q));
  NibbleReg nibblereg_4 (.D({IN3, IN2, IN1, IN0}), .C(and_4_out), .Q(nibblereg_4_q));
  HalfNibReg halfnibreg_1 (.D(ADDRESS), .C(clock_1_out), .Q(A));
  BigMUX bigmux_1 (
    .IN1(nibblereg_2_q), .IN0(nibblereg_1_q), .S(A), .IN3(nibblereg_4_q), .IN2(nibblereg_3_q), .O(bigmux_1_o));
  Clock clock_3 (.out(clock_3_out));
  NibbleReg nibblereg_5 (.D(bigmux_1_o), .C(clock_3_out), .Q(nibblereg_5_q));
  and and_5 (OUT0, nibblereg_5_q[0], M);
  and and_6 (OUT1, nibblereg_5_q[1], M);
  and and_7 (OUT2, nibblereg_5_q[2], M);
  and and_8 (OUT3, nibblereg_5_q[3], M);

  // Notes on the sheet:
  //   261101723
  //   NICHOLAS HAYEK
endmodule

module NibbleReg (
  input  [3:0] D,
  input  C,
  output [3:0] Q
);

  D_Flip_Flop d_ff_1 (.D(D[0]), .clk(C), .Q(Q[0]));  // open: Qn, preset, reset
  D_Flip_Flop d_ff_2 (.D(D[1]), .clk(C), .Q(Q[1]));  // open: Qn, preset, reset
  D_Flip_Flop d_ff_3 (.D(D[2]), .clk(C), .Q(Q[2]));  // open: Qn, preset, reset
  D_Flip_Flop d_ff_4 (.D(D[3]), .clk(C), .Q(Q[3]));  // open: Qn, preset, reset
endmodule

module HalfNibReg (
  input  [1:0] D,
  input  C,
  output [1:0] Q
);

  D_Flip_Flop d_ff_1 (.D(D[0]), .clk(C), .Q(Q[0]));  // open: Qn, preset, reset
  D_Flip_Flop d_ff_2 (.D(D[1]), .clk(C), .Q(Q[1]));  // open: Qn, preset, reset
endmodule

module BigMUX (
  input  [3:0] IN1,
  input  [3:0] IN0,
  input  [1:0] S,
  input  [3:0] IN3,
  input  [3:0] IN2,
  output [3:0] O
);

  wire mydecoder_1_out0, mydecoder_1_out1, mydecoder_1_out2, mydecoder_1_out3;

  MyDecoder mydecoder_1 (
    .S(S), .OUT0(mydecoder_1_out0), .OUT1(mydecoder_1_out1), .OUT2(mydecoder_1_out2), .OUT3(mydecoder_1_out3));
  assign O[0] = mydecoder_1_out0 ? IN0[0] : 1'bz;  // Controlled_Buffer controlled_buffer_1
  assign O[0] = mydecoder_1_out1 ? IN1[0] : 1'bz;  // Controlled_Buffer controlled_buffer_2
  assign O[0] = mydecoder_1_out2 ? IN2[0] : 1'bz;  // Controlled_Buffer controlled_buffer_3
  assign O[0] = mydecoder_1_out3 ? IN3[0] : 1'bz;  // Controlled_Buffer controlled_buffer_4
  assign O[1] = mydecoder_1_out0 ? IN0[1] : 1'bz;  // Controlled_Buffer controlled_buffer_5
  assign O[1] = mydecoder_1_out1 ? IN1[1] : 1'bz;  // Controlled_Buffer controlled_buffer_6
  assign O[1] = mydecoder_1_out2 ? IN2[1] : 1'bz;  // Controlled_Buffer controlled_buffer_7
  assign O[1] = mydecoder_1_out3 ? IN3[1] : 1'bz;  // Controlled_Buffer controlled_buffer_8
  assign O[2] = mydecoder_1_out0 ? IN0[2] : 1'bz;  // Controlled_Buffer controlled_buffer_9
  assign O[2] = mydecoder_1_out1 ? IN1[2] : 1'bz;  // Controlled_Buffer controlled_buffer_10
  assign O[2] = mydecoder_1_out2 ? IN2[2] : 1'bz;  // Controlled_Buffer controlled_buffer_11
  assign O[2] = mydecoder_1_out3 ? IN3[2] : 1'bz;  // Controlled_Buffer controlled_buffer_12
  assign O[3] = mydecoder_1_out0 ? IN0[3] : 1'bz;  // Controlled_Buffer controlled_buffer_13
  assign O[3] = mydecoder_1_out1 ? IN1[3] : 1'bz;  // Controlled_Buffer controlled_buffer_14
  assign O[3] = mydecoder_1_out2 ? IN2[3] : 1'bz;  // Controlled_Buffer controlled_buffer_15
  assign O[3] = mydecoder_1_out3 ? IN3[3] : 1'bz;  // Controlled_Buffer controlled_buffer_16
endmodule

module MyDecoder (
  input  [1:0] S,
  output OUT0,
  output OUT1,
  output OUT2,
  output OUT3
);

  wire not_1_out, not_2_out, not_3_out, not_4_out;

  not not_1 (not_1_out, S[0]);
  not not_2 (not_2_out, S[1]);
  not not_3 (not_3_out, S[1]);
  not not_4 (not_4_out, S[0]);
  and and_1 (OUT0, not_1_out, not_2_out);
  and and_2 (OUT1, S[0], not_3_out);
  and and_3 (OUT2, not_4_out, S[1]);
  and and_4 (OUT3, S[0], S[1]);
endmodule
