// Logisim project SuelynnRAM.circ as structural Verilog: 1 circuit, main circuit main
module main (
  input  Mode,
  input  Address0,
  input  Address1,
  input  Input0,
  input  Input1,
  input  Input2,
  input  Input3,
  output Output0,
  output Output1,
  output Output2,
  output Output3
);

  wire and_1_out, and_2_out, and_3_out, and_4_out, and_5_out, and_6_out, and_7_out, and_8_out, and_9_out,
       and_10_out, and_11_out, and_12_out, and_13_out, and_14_out, and_15_out, and_16_out, and_17_out,
       and_18_out, and_19_out, and_20_out, and_21_out, and_22_out, and_23_out, and_24_out, and_25_out,
       and_26_out, and_27_out, and_28_out, and_29_out, and_30_out, and_31_out, and_32_out, and_33_out,
       and_34_out, and_35_out, and_36_out, and_37_out, and_38_out, and_39_out, and_40_out, and_41_out,
       clock_1_out, d_ff_1_q, d_ff_1_qn, d_ff_2_q, d_ff_3_q, d_ff_4_q, d_ff_5_q, d_ff_6_q, d_ff_7_q,
       d_ff_8_q, d_ff_9_q, d_ff_10_q, d_ff_11_q, d_ff_12_q, d_ff_13_q, d_ff_14_q, d_ff_15_q, d_ff_16_q,
       d_ff_17_q, d_ff_18_q, d_ff_19_q, d_ff_20_q, d_ff_21_q, d_ff_22_q, d_ff_23_q, not_1_out, not_2_out,
       not_3_out, not_4_out, or_1_out, or_2_out, or_3_out, or_4_out;

  Clock clock_1 (.out(clock_1_out));
  D_Flip_Flop d_ff_1 (.D(Mode), .clk(clock_1_out), .Q(d_ff_1_q), .Qn(d_ff_1_qn));  // open: preset, reset
  D_Flip_Flop d_ff_2 (.D(Address0), .clk(clock_1_out), .Q(d_ff_2_q));  // open: Qn, preset, reset
  D_Flip_Flop d_ff_3 (.D(Address1), .clk(clock_1_out), .Q(d_ff_3_q));  // open: Qn, preset, reset
  D_Flip_Flop d_ff_4 (.D(Input0), .clk(clock_1_out), .Q(d_ff_4_q));  // open: Qn, preset, reset
  D_Flip_Flop d_ff_5 (.D(Input1), .clk(clock_1_out), .Q(d_ff_5_q));  // open: Qn, preset, reset
  D_Flip_Flop d_ff_6 (.D(Input2), .clk(clock_1_out), .Q(d_ff_6_q));  // open: Qn, preset, reset
  D_Flip_Flop d_ff_7 (.D(Input3), .clk(clock_1_out), .Q(d_ff_7_q));  // open: Qn, preset, reset
  and and_1 (and_1_out, d_ff_3_q, d_ff_2_q);
  D_Flip_Flop d_ff_8 (.D(d_ff_4_q), .clk(and_2_out), .Q(d_ff_8_q));  // open: Qn, preset, reset
  and and_2 (and_2_out, and_1_out, d_ff_1_qn, clock_1_out);
  D_Flip_Flop d_ff_9 (.D(d_ff_5_q), .clk(and_3_out), .Q(d_ff_9_q));  // open: Qn, preset, reset
  and and_3 (and_3_out, and_1_out, d_ff_1_qn, clock_1_out);
  D_Flip_Flop d_ff_10 (.D(d_ff_6_q), .clk(and_4_out), .Q(d_ff_10_q));  // open: Qn, preset, reset
  and and_4 (and_4_out, and_1_out, d_ff_1_qn, clock_1_out);
  D_Flip_Flop d_ff_11 (.D(d_ff_7_q), .clk(and_5_out), .Q(d_ff_11_q));  // open: Qn, preset, reset
  and and_5 (and_5_out, and_1_out, d_ff_1_qn, clock_1_out);
  and and_6 (and_6_out, and_1_out, d_ff_1_q);
  and and_7 (and_7_out, d_ff_8_q, and_6_out);
  and and_8 (and_8_out, d_ff_9_q, and_6_out);
  and and_9 (and_9_out, d_ff_10_q, and_6_out);
  and and_10 (and_10_out, d_ff_11_q, and_6_out);
  not not_1 (not_1_out, d_ff_2_q);
  and and_11 (and_11_out, d_ff_3_q, not_1_out);
  D_Flip_Flop d_ff_12 (.D(d_ff_4_q), .clk(and_12_out), .Q(d_ff_12_q));  // open: Qn, preset, reset
  and and_12 (and_12_out, and_11_out, d_ff_1_qn, clock_1_out);
  D_Flip_Flop d_ff_13 (.D(d_ff_5_q), .clk(and_13_out), .Q(d_ff_13_q));  // open: Qn, preset, reset
  and and_13 (and_13_out, and_11_out, d_ff_1_qn, clock_1_out);
  D_Flip_Flop d_ff_14 (.D(d_ff_6_q), .clk(and_14_out), .Q(d_ff_14_q));  // open: Qn, preset, reset
  and and_14 (and_14_out, and_11_out, d_ff_1_qn, clock_1_out);
  D_Flip_Flop d_ff_15 (.D(d_ff_7_q), .clk(and_15_out), .Q(d_ff_15_q));  // open: Qn, preset, reset
  and and_15 (and_15_out, and_11_out, d_ff_1_qn, clock_1_out);
  and and_16 (and_16_out, and_11_out, d_ff_1_q);
  and and_17 (and_17_out, d_ff_12_q, and_16_out);
  and and_18 (and_18_out, d_ff_13_q, and_16_out);
  and and_19 (and_19_out, d_ff_14_q, and_16_out);
  and and_20 (and_20_out, d_ff_15_q, and_16_out);
  not not_2 (not_2_out, d_ff_3_q);
  and and_21 (and_21_out, not_2_out, d_ff_2_q);
  D_Flip_Flop d_ff_16 (.D(d_ff_4_q), .clk(and_22_out), .Q(d_ff_16_q));  // open: Qn, preset, reset
  and and_22 (and_22_out, and_21_out, d_ff_1_qn, clock_1_out);
  D_Flip_Flop d_ff_17 (.D(d_ff_5_q), .clk(and_23_out), .Q(d_ff_17_q));  // open: Qn, preset, reset
  and and_23 (and_23_out, and_21_out, d_ff_1_qn, clock_1_out);
  D_Flip_Flop d_ff_18 (.D(d_ff_6_q), .clk(and_24_out), .Q(d_ff_18_q));  // open: Qn, preset, reset
  and and_24 (and_24_out, and_21_out, d_ff_1_qn, clock_1_out);
  D_Flip_Flop d_ff_19 (.D(d_ff_7_q), .clk(and_25_out), .Q(d_ff_19_q));  // open: Qn, preset, reset
  and and_25 (and_25_out, and_21_out, d_ff_1_qn, clock_1_out);
  and and_26 (and_26_out, and_21_out, d_ff_1_q);
  and and_27 (and_27_out, d_ff_16_q, and_26_out);
  and and_28 (and_28_out, d_ff_17_q, and_26_out);
  and and_29 (and_29_out, d_ff_18_q, and_26_out);
  and and_30 (and_30_out, d_ff_19_q, and_26_out);
  not not_3 (not_3_out, d_ff_3_q);
  not not_4 (not_4_out, d_ff_2_q);
  and and_31 (and_31_out, not_3_out, not_4_out);
  D_Flip_Flop d_ff_20 (.D(d_ff_4_q), .clk(and_32_out), .Q(d_ff_20_q));  // open: Qn, preset, reset
  and and_32 (and_32_out, and_31_out, d_ff_1_qn, clock_1_out);
  D_Flip_Flop d_ff_21 (.D(d_ff_5_q), .clk(and_33_out), .Q(d_ff_21_q));  // open: Qn, preset, reset
  and and_33 (and_33_out, and_31_out, d_ff_1_qn, clock_1_out);
  D_Flip_Flop d_ff_22 (.D(d_ff_6_q), .clk(and_34_out), .Q(d_ff_22_q));  // open: Qn, preset, reset
  and and_34 (and_34_out, and_31_out, d_ff_1_qn, clock_1_out);
  D_Flip_Flop d_ff_23 (.D(d_ff_7_q), .clk(and_35_out), .Q(d_ff_23_q));  // open: Qn, preset, reset
  and and_35 (and_35_out, and_31_out, d_ff_1_qn, clock_1_out);
  and and_36 (and_36_out, and_31_out, d_ff_1_q);
  and and_37 (and_37_out, d_ff_20_q, and_36_out);
  and and_38 (and_38_out, d_ff_21_q, and_36_out);
  and and_39 (and_39_out, d_ff_22_q, and_36_out);
  and and_40 (and_40_out, d_ff_23_q, and_36_out);
  or or_1 (or_1_out, and_37_out, and_27_out, and_17_out, and_7_out);
  or or_2 (or_2_out, and_38_out, and_28_out, and_18_out, and_8_out);
  or or_3 (or_3_out, and_39_out, and_29_out, and_19_out, and_9_out);
  or or_4 (or_4_out, and_40_out, and_30_out, and_20_out, and_10_out);
  and and_41 (and_41_out, d_ff_1_q, clock_1_out);
  D_Flip_Flop d_ff_24 (.D(or_1_out), .clk(and_41_out), .Q(Output0));  // open: Qn, preset, reset
  D_Flip_Flop d_ff_25 (.D(or_2_out), .clk(and_41_out), .Q(Output1));  // open: Qn, preset, reset
  D_Flip_Flop d_ff_26 (.D(or_3_out), .clk(and_41_out), .Q(Output2));  // open: Qn, preset, reset
  D_Flip_Flop d_ff_27 (.D(or_4_out), .clk(and_41_out), .Q(Output3));  // open: Qn, preset, reset

  // Notes on the sheet:
  //   Name: Suelynn Lee
  //   Student ID: 261090996
  //   Address3
  //   Address3
  //   Address3
  //   Address3
  //   Address2
  //   Address2
  //   Address2
  //   Address2
  //   Address1
  //   Address1
  //   Address1
  //   Address1
  //   Address0
  //   Address0
  //   Address0
  //   Address0
endmodule
