// Logisim project project.circ as structural Verilog: 7 circuits, main circuit main
module main (
  input  manual_override,
  input  in_2,
  input  manual_cycle,
  input  in_4,
  input  read,
  input  manual_cycle_2,
  input  address,
  input  in_8,
  input  \input ,
  input  in_10,
  input  in_11,
  input  [2:0] address_2,
  input  [3:0] input_2,
  input  in_14
);

  wire ADD, and_2_out, and_4_out, and_5_out, and_6_out, BINV, bitA, bitB, bitC, bitD, C, clock_1_out,
       d_ff_1_qn, d_ff_2_q, d_ff_2_qn, d_ff_3_qn, d_ff_4_q, d_ff_4_qn, d_ff_5_qn, DATAA, DATAW,
       decoder_1_out0, decoder_1_out1, HALT, LOAD, multiplexer_6_out, multiplexer_7_out, not_1_out,
       not_2_out, not_3_out, or_1_out, or_2_out, READA, READB, SAVE, SUB, WENAB, WSELE, xor_1_out, xor_2_out,
       xor_3_out;
  wire [2:0] d_ff_1_q, multiplexer_1_out, myalucomb_1_status0_sign, register_1_q;
  wire [3:0] multiplexer_2_out, multiplexer_3_out, multiplexer_4_out, multiplexer_5_out, myalucomb_1_result0,
       ram2nibble_1_output0, ram8nibble_1_output0, register_3_q, register_4_q, register_5_q, register_6_q,
       register_7_q;

  not not_1 (not_1_out, HALT);
  Register #(.width(3)) register_1 (.D(d_ff_1_q), .clk(xor_1_out), .Q(register_1_q));  // open: en, clr
  xor xor_1 (xor_1_out, in_14, C);
  Clock clock_1 (.out(clock_1_out));
  and and_1 (C, clock_1_out, or_1_out);
  or or_1 (or_1_out, not_1_out, in_4);
  Multiplexer #(.width(3)) multiplexer_1 (.in0(register_1_q), .in1(address_2), .out(multiplexer_1_out), .sel(in_2));
  D_Flip_Flop #(.trigger("falling")) d_ff_1 (
    .D(d_ff_1_qn), .clk(and_2_out), .Q(d_ff_1_q[0]), .Qn(d_ff_1_qn));  // open: preset, reset
  and and_2 (and_2_out, d_ff_4_q, d_ff_2_q);
  D_Flip_Flop #(.trigger("falling")) d_ff_2 (
    .D(d_ff_2_qn), .clk(xor_1_out), .Q(d_ff_2_q), .Qn(d_ff_2_qn));  // open: preset, reset
  // Probe on address_2
  // Probe on d_ff_1_q[0]
  D_Flip_Flop #(.trigger("falling")) d_ff_3 (
    .D(d_ff_3_qn), .clk(d_ff_1_q[0]), .Q(d_ff_1_q[1]), .Qn(d_ff_3_qn));  // open: preset, reset
  D_Flip_Flop #(.trigger("falling")) d_ff_4 (
    .D(d_ff_4_qn), .clk(d_ff_2_q), .Q(d_ff_4_q), .Qn(d_ff_4_qn));  // open: preset, reset
  xor xor_2 (xor_2_out, manual_cycle_2, C);
  not not_2 (not_2_out, in_2);
  // Probe on d_ff_1_q[1]
  D_Flip_Flop #(.trigger("falling")) d_ff_5 (
    .D(d_ff_5_qn), .clk(d_ff_1_q[1]), .Q(d_ff_1_q[2]), .Qn(d_ff_5_qn));  // open: preset, reset
  // Probe on d_ff_1_q[2]
  Ram8Nibble ram8nibble_1 (
    .C(xor_2_out), .Mode(not_2_out), .Address0(multiplexer_1_out[0]), .Address1(multiplexer_1_out[1]),
    .Address2(multiplexer_1_out[2]), .Input3(input_2[3]), .Input2(input_2[2]), .Input1(input_2[1]),
    .Input0(input_2[0]), .Output3(ram8nibble_1_output0[3]), .Output2(ram8nibble_1_output0[2]),
    .Output1(ram8nibble_1_output0[1]), .Output0(ram8nibble_1_output0[0]));
  and and_3 (HALT, bitA, bitB, bitC, bitD);
  Register #(.width(4)) register_2 (
    .D(ram8nibble_1_output0), .clk(xor_2_out), .Q({bitA, bitB, bitC, bitD}));  // open: en, clr
  Decoder #(.enable("false")) decoder_1 (.out0(decoder_1_out0), .out1(decoder_1_out1), .sel(WSELE));
  Decoder #(.enable("false"), .select(2)) decoder_2 (
    .out0(LOAD), .out1(SAVE), .out2(ADD), .out3(SUB), .sel({bitA, bitB}));
  and and_4 (and_4_out, C, WENAB);
  Register #(.width(4)) register_3 (.D(multiplexer_4_out), .clk(and_5_out), .Q(register_3_q));  // open: en, clr
  and and_5 (and_5_out, and_4_out, decoder_1_out0);
  Register #(.width(4)) register_4 (.D(multiplexer_4_out), .clk(and_6_out), .Q(register_4_q));  // open: en, clr
  and and_6 (and_6_out, and_4_out, decoder_1_out1);
  // Probe on register_3_q
  // Probe on register_4_q
  Multiplexer #(.width(4)) multiplexer_2 (.in0(register_3_q), .in1(register_4_q), .out(multiplexer_2_out), .sel(READA));
  Multiplexer #(.width(4)) multiplexer_3 (.in0(register_3_q), .in1(register_4_q), .out(multiplexer_3_out), .sel(READB));
  CU cu_1 (
    .bitC(bitC), .bitD(bitD), .LOAD(LOAD), .SAVE(SAVE), .ADD(ADD), .SUB(SUB), .BINV(BINV), .DATAA(DATAA),
    .READB(READB), .READA(READA), .WSELE(WSELE), .WENAB(WENAB), .DATAW(DATAW));
  // Probe on myalucomb_1_result0
  Register #(.width(4)) register_5 (.D(myalucomb_1_result0), .clk(C), .Q(register_5_q));  // open: en, clr
  MyALUComb myalucomb_1 (
    .Operation1(1'b1), .AInvert(1'b0), .BInvert(BINV), .Operation0(1'b0), .A0(multiplexer_2_out[0]),
    .B0(multiplexer_3_out[0]), .A1(multiplexer_2_out[1]), .B1(multiplexer_3_out[1]),
    .A2(multiplexer_2_out[2]), .B2(multiplexer_3_out[2]), .A3(multiplexer_2_out[3]),
    .B3(multiplexer_3_out[3]), .Result0(myalucomb_1_result0[0]), .Result1(myalucomb_1_result0[1]),
    .Result2(myalucomb_1_result0[2]), .Result3(myalucomb_1_result0[3]),
    .Status0_Sign(myalucomb_1_status0_sign[0]), .Status1_Zero(myalucomb_1_status0_sign[1]),
    .Status2_SignOverflow(myalucomb_1_status0_sign[2]));
  Register #(.width(4)) register_6 (.D(register_5_q), .clk(C), .Q(register_6_q));  // open: en, clr
  // Probe on myalucomb_1_status0_sign
  Register #(.width(4)) register_7 (.D(register_6_q), .clk(C), .Q(register_7_q));  // open: en, clr
  Multiplexer #(.width(4)) multiplexer_4 (
    .in0(ram2nibble_1_output0), .in1(register_7_q), .out(multiplexer_4_out), .sel(or_2_out));
  or or_2 (or_2_out, SUB, ADD);
  // Probe on {in_8, \input , in_10, in_11}
  Multiplexer #(.width(4)) multiplexer_5 (
    .in0(multiplexer_2_out), .in1({in_8, \input , in_10, in_11}), .out(multiplexer_5_out),
    .sel(manual_override));
  xor xor_3 (xor_3_out, manual_cycle, C);
  not not_3 (not_3_out, DATAW);
  Multiplexer multiplexer_6 (.in0(not_3_out), .in1(read), .out(multiplexer_6_out), .sel(manual_override));
  Multiplexer multiplexer_7 (.in0(DATAA), .in1(address), .out(multiplexer_7_out), .sel(manual_override));
  Ram2Nibble ram2nibble_1 (
    .C(xor_3_out), .Mode(multiplexer_6_out), .Address0(multiplexer_7_out), .Input3(multiplexer_5_out[3]),
    .Input2(multiplexer_5_out[2]), .Input1(multiplexer_5_out[1]), .Input0(multiplexer_5_out[0]),
    .Output3(ram2nibble_1_output0[3]), .Output2(ram2nibble_1_output0[2]), .Output1(ram2nibble_1_output0[1]),
    .Output0(ram2nibble_1_output0[0]));
  // Probe on ram2nibble_1_output0

  // Other names for the same wires on the sheet: overrideHalt = in_4; setInstructions = in_2

  // Notes on the sheet:
  //   CP
  //   manual cycle
  //   Counter
  //   Instruction RAM
  //   IR
  //   Write Select
  //   Write Data
  //   R0
  //   R1
  //   note: register will load with back-logged ALU register before instruction cycle is over.
  //   Maybe we can use controlled buffer to make the data go through when 4 ticks happened, increasing the counter?
  //   ALU Out
  //   Register file is overwritten in the middle of the instruction
  //   ALU Status
  //   Data RAM
endmodule

module MyALU (
  input  C,
  input  Operation1,
  input  AInvert,
  input  BInvert,
  input  Operation0,
  input  A0,
  input  B0,
  input  A1,
  input  B1,
  input  A2,
  input  B2,
  input  A3,
  input  B3,
  output Result0,
  output Result1,
  output Result2,
  output Result3,
  output Status0_Sign,
  output Status1_Zero,
  output Status2_SignOverflow
);

  wire and_1_out, and_2_out, and_3_out, and_4_out, and_5_out, and_6_out, and_7_out, and_8_out, and_9_out,
       and_10_out, and_11_out, and_12_out, and_13_out, and_14_out, and_15_out, and_16_out, and_17_out,
       and_18_out, and_19_out, and_20_out, and_21_out, and_22_out, and_23_out, and_24_out, and_25_out,
       and_26_out, and_27_out, and_28_out, and_29_out, and_30_out, and_31_out, and_32_out, and_33_out,
       and_34_out, and_35_out, and_36_out, and_37_out, and_38_out, and_39_out, and_40_out, and_41_out,
       and_42_out, and_43_out, and_44_out, and_45_out, and_46_out, and_47_out, and_48_out, and_49_out,
       and_50_out, and_51_out, and_52_out, and_53_out, and_54_out, and_55_out, d_ff_1_q, d_ff_2_q, d_ff_3_q,
       d_ff_4_q, d_ff_5_q, d_ff_6_q, d_ff_7_q, d_ff_8_q, not_1_out, not_2_out, not_3_out, not_4_out,
       not_5_out, not_6_out, not_7_out, not_8_out, not_9_out, not_10_out, not_11_out, not_12_out, not_13_out,
       not_14_out, not_15_out, not_16_out, not_17_out, not_18_out, not_19_out, not_20_out, not_21_out,
       not_22_out, or_1_out, or_2_out, or_3_out, or_4_out, or_5_out, or_6_out, or_7_out, or_8_out, or_9_out,
       or_10_out, or_11_out, or_13_out, or_14_out, or_15_out, or_16_out, or_17_out, or_18_out, or_19_out,
       or_20_out, or_21_out, or_22_out, or_23_out, or_24_out, or_25_out, xor_1_out, xor_2_out, xor_3_out,
       xor_4_out, xor_5_out, xor_6_out, xor_7_out, xor_8_out, xor_9_out, xor_10_out;

  D_Flip_Flop d_ff_1 (.D(A0), .clk(C), .Q(d_ff_1_q));  // open: Qn, preset, reset
  D_Flip_Flop d_ff_2 (.D(B0), .clk(C), .Q(d_ff_2_q));  // open: Qn, preset, reset
  D_Flip_Flop d_ff_3 (.D(A1), .clk(C), .Q(d_ff_3_q));  // open: Qn, preset, reset
  D_Flip_Flop d_ff_4 (.D(B1), .clk(C), .Q(d_ff_4_q));  // open: Qn, preset, reset
  D_Flip_Flop d_ff_5 (.D(A2), .clk(C), .Q(d_ff_5_q));  // open: Qn, preset, reset
  D_Flip_Flop d_ff_6 (.D(B2), .clk(C), .Q(d_ff_6_q));  // open: Qn, preset, reset
  D_Flip_Flop d_ff_7 (.D(A3), .clk(C), .Q(d_ff_7_q));  // open: Qn, preset, reset
  D_Flip_Flop d_ff_8 (.D(B3), .clk(C), .Q(d_ff_8_q));  // open: Qn, preset, reset
  not not_1 (not_1_out, d_ff_1_q);
  not not_2 (not_2_out, d_ff_2_q);
  not not_3 (not_3_out, d_ff_3_q);
  not not_4 (not_4_out, d_ff_4_q);
  not not_5 (not_5_out, d_ff_5_q);
  not not_6 (not_6_out, d_ff_6_q);
  not not_7 (not_7_out, d_ff_7_q);
  not not_8 (not_8_out, d_ff_8_q);
  and and_1 (and_1_out, d_ff_1_q, not_9_out);
  not not_9 (not_9_out, AInvert);
  and and_2 (and_2_out, AInvert, not_1_out);
  and and_3 (and_3_out, d_ff_2_q, not_10_out);
  not not_10 (not_10_out, BInvert);
  and and_4 (and_4_out, BInvert, not_2_out);
  and and_5 (and_5_out, d_ff_3_q, not_11_out);
  not not_11 (not_11_out, AInvert);
  and and_6 (and_6_out, AInvert, not_3_out);
  and and_7 (and_7_out, d_ff_4_q, not_12_out);
  not not_12 (not_12_out, BInvert);
  and and_8 (and_8_out, BInvert, not_4_out);
  and and_9 (and_9_out, d_ff_5_q, not_13_out);
  not not_13 (not_13_out, AInvert);
  and and_10 (and_10_out, AInvert, not_5_out);
  and and_11 (and_11_out, d_ff_6_q, not_14_out);
  not not_14 (not_14_out, BInvert);
  and and_12 (and_12_out, BInvert, not_6_out);
  and and_13 (and_13_out, d_ff_7_q, not_15_out);
  not not_15 (not_15_out, AInvert);
  and and_14 (and_14_out, AInvert, not_7_out);
  and and_15 (and_15_out, d_ff_8_q, not_16_out);
  not not_16 (not_16_out, BInvert);
  and and_16 (and_16_out, BInvert, not_8_out);
  or or_1 (or_1_out, and_1_out, and_2_out);
  or or_2 (or_2_out, and_3_out, and_4_out);
  or or_3 (or_3_out, and_5_out, and_6_out);
  or or_4 (or_4_out, and_7_out, and_8_out);
  or or_5 (or_5_out, and_9_out, and_10_out);
  or or_6 (or_6_out, and_11_out, and_12_out);
  or or_7 (or_7_out, and_13_out, and_14_out);
  or or_8 (or_8_out, and_15_out, and_16_out);
  xor xor_1 (xor_1_out, or_1_out, or_2_out);
  and and_17 (and_17_out, or_2_out, or_1_out);
  xor xor_2 (xor_2_out, or_3_out, or_4_out);
  and and_18 (and_18_out, or_4_out, or_3_out);
  xor xor_3 (xor_3_out, or_5_out, or_6_out);
  and and_19 (and_19_out, or_6_out, or_5_out);
  xor xor_4 (xor_4_out, or_7_out, or_8_out);
  and and_20 (and_20_out, or_8_out, or_7_out);
  xor xor_5 (xor_5_out, BInvert, xor_1_out);
  and and_21 (and_21_out, xor_1_out, BInvert);
  xor xor_6 (xor_6_out, or_9_out, xor_2_out);
  and and_22 (and_22_out, xor_2_out, or_9_out);
  xor xor_7 (xor_7_out, or_10_out, xor_3_out);
  and and_23 (and_23_out, xor_3_out, or_10_out);
  xor xor_8 (xor_8_out, or_11_out, xor_4_out);
  and and_24 (and_24_out, xor_4_out, or_11_out);
  or or_9 (or_9_out, and_21_out, and_17_out);
  or or_10 (or_10_out, and_22_out, and_18_out);
  or or_11 (or_11_out, and_23_out, and_19_out);
  // OR_Gate or_12 has open pins: in0=and_24_out, in1=and_20_out, out=open
  not not_17 (not_17_out, Operation1);
  or or_13 (or_13_out, or_1_out, or_2_out);
  and and_25 (and_25_out, or_1_out, or_2_out);
  or or_14 (or_14_out, or_3_out, or_4_out);
  and and_26 (and_26_out, or_3_out, or_4_out);
  or or_15 (or_15_out, or_5_out, or_6_out);
  and and_27 (and_27_out, or_5_out, or_6_out);
  or or_16 (or_16_out, or_7_out, or_8_out);
  and and_28 (and_28_out, or_7_out, or_8_out);
  not not_18 (not_18_out, Operation0);
  and and_29 (and_29_out, xor_5_out, Operation1);
  and and_30 (and_30_out, or_13_out, not_17_out);
  and and_31 (and_31_out, and_25_out, not_17_out);
  and and_32 (and_32_out, xor_6_out, Operation1);
  and and_33 (and_33_out, or_14_out, not_17_out);
  and and_34 (and_34_out, and_26_out, not_17_out);
  and and_35 (and_35_out, xor_7_out, Operation1);
  and and_36 (and_36_out, or_15_out, not_17_out);
  and and_37 (and_37_out, and_27_out, not_17_out);
  and and_38 (and_38_out, xor_8_out, Operation1);
  and and_39 (and_39_out, or_16_out, not_17_out);
  and and_40 (and_40_out, and_28_out, not_17_out);
  and and_41 (and_41_out, and_29_out, not_18_out);
  and and_42 (and_42_out, Operation0, and_30_out);
  and and_43 (and_43_out, not_18_out, and_31_out);
  and and_44 (and_44_out, and_32_out, not_18_out);
  and and_45 (and_45_out, Operation0, and_33_out);
  and and_46 (and_46_out, not_18_out, and_34_out);
  and and_47 (and_47_out, and_35_out, not_18_out);
  and and_48 (and_48_out, Operation0, and_36_out);
  and and_49 (and_49_out, not_18_out, and_37_out);
  and and_50 (and_50_out, and_38_out, not_18_out);
  and and_51 (and_51_out, Operation0, and_39_out);
  and and_52 (and_52_out, not_18_out, and_40_out);
  or or_17 (or_17_out, and_41_out, and_42_out);
  or or_18 (or_18_out, and_44_out, and_45_out);
  or or_19 (or_19_out, and_47_out, and_48_out);
  or or_20 (or_20_out, and_50_out, and_51_out);
  or or_21 (or_21_out, or_17_out, and_43_out);
  or or_22 (or_22_out, or_18_out, and_46_out);
  or or_23 (or_23_out, or_19_out, and_49_out);
  or or_24 (or_24_out, or_20_out, and_52_out);
  D_Flip_Flop d_ff_9 (.D(or_21_out), .clk(C), .Q(Result0));  // open: Qn, preset, reset
  D_Flip_Flop d_ff_10 (.D(or_22_out), .clk(C), .Q(Result1));  // open: Qn, preset, reset
  D_Flip_Flop d_ff_11 (.D(or_23_out), .clk(C), .Q(Result2));  // open: Qn, preset, reset
  D_Flip_Flop d_ff_12 (.D(or_24_out), .clk(C), .Q(Result3));  // open: Qn, preset, reset
  xor xor_9 (xor_9_out, or_7_out, or_8_out);
  and and_53 (and_53_out, or_7_out, or_8_out);
  and and_54 (and_54_out, or_24_out, xor_9_out);
  not not_19 (not_19_out, or_21_out);
  not not_20 (not_20_out, or_22_out);
  not not_21 (not_21_out, or_23_out);
  not not_22 (not_22_out, or_24_out);
  or or_25 (or_25_out, and_54_out, and_53_out);
  and and_55 (and_55_out, not_19_out, not_20_out, not_21_out, not_22_out);
  xor xor_10 (xor_10_out, or_24_out, or_25_out);
  D_Flip_Flop d_ff_13 (.D(or_25_out), .clk(C), .Q(Status0_Sign));  // open: Qn, preset, reset
  D_Flip_Flop d_ff_14 (.D(and_55_out), .clk(C), .Q(Status1_Zero));  // open: Qn, preset, reset
  D_Flip_Flop d_ff_15 (.D(xor_10_out), .clk(C), .Q(Status2_SignOverflow));  // open: Qn, preset, reset

  // Notes on the sheet:
  //   A0: initial=0x1
  //   B0: initial=0x1
  //   Multiplexor for inverting
  //    Full bit adder circuit
  //   Multiplexer to choose operation
endmodule

module Ram8Nibble (
  input  C,
  input  Mode,
  input  Address0,
  input  Address1,
  input  Address2,
  input  Input3,
  input  Input2,
  input  Input1,
  input  Input0,
  output Output3,
  output Output2,
  output Output1,
  output Output0
);

  wire and_1_out, and_2_out, and_3_out, and_4_out, and_5_out, and_6_out, and_7_out, and_8_out, and_9_out,
       and_10_out, and_11_out, and_12_out, and_13_out, and_14_out, and_15_out, and_16_out, and_17_out,
       and_18_out, and_19_out, and_20_out, and_21_out, and_22_out, and_23_out, and_24_out, and_25_out,
       and_26_out, and_27_out, and_28_out, and_29_out, and_30_out, and_31_out, and_32_out, and_33_out,
       and_34_out, and_35_out, and_36_out, and_37_out, and_38_out, and_39_out, and_40_out, and_41_out,
       and_42_out, and_43_out, and_44_out, and_45_out, and_46_out, and_47_out, and_48_out, and_49_out,
       and_50_out, and_51_out, and_52_out, and_53_out, and_54_out, and_55_out, and_56_out, and_57_out,
       and_58_out, and_59_out, and_60_out, and_61_out, and_62_out, and_63_out, and_64_out, and_65_out,
       and_66_out, and_67_out, and_68_out, and_69_out, and_70_out, and_71_out, and_72_out, and_73_out,
       and_74_out, and_75_out, and_76_out, and_77_out, and_78_out, and_79_out, and_80_out, and_81_out,
       d_ff_1_q, d_ff_1_qn, d_ff_2_q, d_ff_3_q, d_ff_4_q, d_ff_5_q, d_ff_6_q, d_ff_7_q, d_ff_8_q, d_ff_9_q,
       d_ff_10_q, d_ff_11_q, d_ff_12_q, d_ff_13_q, d_ff_14_q, d_ff_15_q, d_ff_16_q, d_ff_17_q, d_ff_18_q,
       d_ff_19_q, d_ff_20_q, d_ff_21_q, d_ff_22_q, d_ff_23_q, d_ff_24_q, d_ff_25_q, d_ff_26_q, d_ff_27_q,
       d_ff_28_q, d_ff_29_q, d_ff_30_q, d_ff_31_q, d_ff_32_q, d_ff_33_q, d_ff_34_q, d_ff_35_q, d_ff_36_q,
       d_ff_37_q, d_ff_38_q, d_ff_39_q, d_ff_40_q, not_1_out, not_2_out, not_3_out, not_4_out, not_5_out,
       not_6_out, not_7_out, not_8_out, not_9_out, not_10_out, not_11_out, not_12_out, or_1_out, or_2_out,
       or_3_out, or_4_out;

  D_Flip_Flop d_ff_1 (.D(Mode), .clk(C), .Q(d_ff_1_q), .Qn(d_ff_1_qn));  // open: preset, reset
  D_Flip_Flop d_ff_2 (.D(Address0), .clk(C), .Q(d_ff_2_q));  // open: Qn, preset, reset
  D_Flip_Flop d_ff_3 (.D(Address1), .clk(C), .Q(d_ff_3_q));  // open: Qn, preset, reset
  D_Flip_Flop d_ff_4 (.D(Address2), .clk(C), .Q(d_ff_4_q));  // open: Qn, preset, reset
  D_Flip_Flop d_ff_5 (.D(Input3), .clk(C), .Q(d_ff_5_q));  // open: Qn, preset, reset
  D_Flip_Flop d_ff_6 (.D(Input2), .clk(C), .Q(d_ff_6_q));  // open: Qn, preset, reset
  D_Flip_Flop d_ff_7 (.D(Input1), .clk(C), .Q(d_ff_7_q));  // open: Qn, preset, reset
  D_Flip_Flop d_ff_8 (.D(Input0), .clk(C), .Q(d_ff_8_q));  // open: Qn, preset, reset
  and and_1 (and_1_out, d_ff_4_q, d_ff_3_q, d_ff_2_q);
  D_Flip_Flop d_ff_9 (.D(d_ff_5_q), .clk(and_2_out), .Q(d_ff_9_q));  // open: Qn, preset, reset
  and and_2 (and_2_out, and_1_out, d_ff_1_qn, C);
  D_Flip_Flop d_ff_10 (.D(d_ff_6_q), .clk(and_3_out), .Q(d_ff_10_q));  // open: Qn, preset, reset
  and and_3 (and_3_out, and_1_out, d_ff_1_qn, C);
  D_Flip_Flop d_ff_11 (.D(d_ff_7_q), .clk(and_4_out), .Q(d_ff_11_q));  // open: Qn, preset, reset
  and and_4 (and_4_out, and_1_out, d_ff_1_qn, C);
  D_Flip_Flop d_ff_12 (.D(d_ff_8_q), .clk(and_5_out), .Q(d_ff_12_q));  // open: Qn, preset, reset
  and and_5 (and_5_out, and_1_out, d_ff_1_qn, C);
  and and_6 (and_6_out, and_1_out, d_ff_1_q);
  and and_7 (and_7_out, d_ff_9_q, and_6_out);
  and and_8 (and_8_out, d_ff_10_q, and_6_out);
  and and_9 (and_9_out, d_ff_11_q, and_6_out);
  and and_10 (and_10_out, d_ff_12_q, and_6_out);
  not not_1 (not_1_out, d_ff_2_q);
  and and_11 (and_11_out, d_ff_4_q, d_ff_3_q, not_1_out);
  D_Flip_Flop d_ff_13 (.D(d_ff_5_q), .clk(and_12_out), .Q(d_ff_13_q));  // open: Qn, preset, reset
  and and_12 (and_12_out, and_11_out, d_ff_1_qn, C);
  D_Flip_Flop d_ff_14 (.D(d_ff_6_q), .clk(and_13_out), .Q(d_ff_14_q));  // open: Qn, preset, reset
  and and_13 (and_13_out, and_11_out, d_ff_1_qn, C);
  D_Flip_Flop d_ff_15 (.D(d_ff_7_q), .clk(and_14_out), .Q(d_ff_15_q));  // open: Qn, preset, reset
  and and_14 (and_14_out, and_11_out, d_ff_1_qn, C);
  D_Flip_Flop d_ff_16 (.D(d_ff_8_q), .clk(and_15_out), .Q(d_ff_16_q));  // open: Qn, preset, reset
  and and_15 (and_15_out, and_11_out, d_ff_1_qn, C);
  and and_16 (and_16_out, and_11_out, d_ff_1_q);
  and and_17 (and_17_out, d_ff_13_q, and_16_out);
  and and_18 (and_18_out, d_ff_14_q, and_16_out);
  and and_19 (and_19_out, d_ff_15_q, and_16_out);
  and and_20 (and_20_out, d_ff_16_q, and_16_out);
  not not_2 (not_2_out, d_ff_3_q);
  and and_21 (and_21_out, d_ff_4_q, not_2_out, d_ff_2_q);
  D_Flip_Flop d_ff_17 (.D(d_ff_5_q), .clk(and_22_out), .Q(d_ff_17_q));  // open: Qn, preset, reset
  and and_22 (and_22_out, and_21_out, d_ff_1_qn, C);
  D_Flip_Flop d_ff_18 (.D(d_ff_6_q), .clk(and_23_out), .Q(d_ff_18_q));  // open: Qn, preset, reset
  and and_23 (and_23_out, and_21_out, d_ff_1_qn, C);
  D_Flip_Flop d_ff_19 (.D(d_ff_7_q), .clk(and_24_out), .Q(d_ff_19_q));  // open: Qn, preset, reset
  and and_24 (and_24_out, and_21_out, d_ff_1_qn, C);
  D_Flip_Flop d_ff_20 (.D(d_ff_8_q), .clk(and_25_out), .Q(d_ff_20_q));  // open: Qn, preset, reset
  and and_25 (and_25_out, and_21_out, d_ff_1_qn, C);
  and and_26 (and_26_out, and_21_out, d_ff_1_q);
  and and_27 (and_27_out, d_ff_17_q, and_26_out);
  and and_28 (and_28_out, d_ff_18_q, and_26_out);
  and and_29 (and_29_out, d_ff_19_q, and_26_out);
  and and_30 (and_30_out, d_ff_20_q, and_26_out);
  not not_3 (not_3_out, d_ff_3_q);
  not not_4 (not_4_out, d_ff_2_q);
  and and_31 (and_31_out, d_ff_4_q, not_3_out, not_4_out);
  D_Flip_Flop d_ff_21 (.D(d_ff_5_q), .clk(and_32_out), .Q(d_ff_21_q));  // open: Qn, preset, reset
  and and_32 (and_32_out, and_31_out, d_ff_1_qn, C);
  D_Flip_Flop d_ff_22 (.D(d_ff_6_q), .clk(and_33_out), .Q(d_ff_22_q));  // open: Qn, preset, reset
  and and_33 (and_33_out, and_31_out, d_ff_1_qn, C);
  D_Flip_Flop d_ff_23 (.D(d_ff_7_q), .clk(and_34_out), .Q(d_ff_23_q));  // open: Qn, preset, reset
  and and_34 (and_34_out, and_31_out, d_ff_1_qn, C);
  D_Flip_Flop d_ff_24 (.D(d_ff_8_q), .clk(and_35_out), .Q(d_ff_24_q));  // open: Qn, preset, reset
  and and_35 (and_35_out, and_31_out, d_ff_1_qn, C);
  and and_36 (and_36_out, and_31_out, d_ff_1_q);
  and and_37 (and_37_out, d_ff_21_q, and_36_out);
  and and_38 (and_38_out, d_ff_22_q, and_36_out);
  and and_39 (and_39_out, d_ff_23_q, and_36_out);
  and and_40 (and_40_out, d_ff_24_q, and_36_out);
  not not_5 (not_5_out, d_ff_4_q);
  and and_41 (and_41_out, not_5_out, d_ff_3_q, d_ff_2_q);
  D_Flip_Flop d_ff_25 (.D(d_ff_5_q), .clk(and_42_out), .Q(d_ff_25_q));  // open: Qn, preset, reset
  and and_42 (and_42_out, and_41_out, d_ff_1_qn, C);
  D_Flip_Flop d_ff_26 (.D(d_ff_6_q), .clk(and_43_out), .Q(d_ff_26_q));  // open: Qn, preset, reset
  and and_43 (and_43_out, and_41_out, d_ff_1_qn, C);
  D_Flip_Flop d_ff_27 (.D(d_ff_7_q), .clk(and_44_out), .Q(d_ff_27_q));  // open: Qn, preset, reset
  and and_44 (and_44_out, and_41_out, d_ff_1_qn, C);
  D_Flip_Flop d_ff_28 (.D(d_ff_8_q), .clk(and_45_out), .Q(d_ff_28_q));  // open: Qn, preset, reset
  and and_45 (and_45_out, and_41_out, d_ff_1_qn, C);
  and and_46 (and_46_out, and_41_out, d_ff_1_q);
  and and_47 (and_47_out, d_ff_25_q, and_46_out);
  and and_48 (and_48_out, d_ff_26_q, and_46_out);
  and and_49 (and_49_out, d_ff_27_q, and_46_out);
  and and_50 (and_50_out, d_ff_28_q, and_46_out);
  not not_6 (not_6_out, d_ff_4_q);
  not not_7 (not_7_out, d_ff_2_q);
  and and_51 (and_51_out, not_6_out, d_ff_3_q, not_7_out);
  D_Flip_Flop d_ff_29 (.D(d_ff_5_q), .clk(and_52_out), .Q(d_ff_29_q));  // open: Qn, preset, reset
  and and_52 (and_52_out, and_51_out, d_ff_1_qn, C);
  D_Flip_Flop d_ff_30 (.D(d_ff_6_q), .clk(and_53_out), .Q(d_ff_30_q));  // open: Qn, preset, reset
  and and_53 (and_53_out, and_51_out, d_ff_1_qn, C);
  D_Flip_Flop d_ff_31 (.D(d_ff_7_q), .clk(and_54_out), .Q(d_ff_31_q));  // open: Qn, preset, reset
  and and_54 (and_54_out, and_51_out, d_ff_1_qn, C);
  D_Flip_Flop d_ff_32 (.D(d_ff_8_q), .clk(and_55_out), .Q(d_ff_32_q));  // open: Qn, preset, reset
  and and_55 (and_55_out, and_51_out, d_ff_1_qn, C);
  and and_56 (and_56_out, and_51_out, d_ff_1_q);
  and and_57 (and_57_out, d_ff_29_q, and_56_out);
  and and_58 (and_58_out, d_ff_30_q, and_56_out);
  and and_59 (and_59_out, d_ff_31_q, and_56_out);
  and and_60 (and_60_out, d_ff_32_q, and_56_out);
  not not_8 (not_8_out, d_ff_4_q);
  not not_9 (not_9_out, d_ff_3_q);
  and and_61 (and_61_out, not_8_out, not_9_out, d_ff_2_q);
  D_Flip_Flop d_ff_33 (.D(d_ff_5_q), .clk(and_62_out), .Q(d_ff_33_q));  // open: Qn, preset, reset
  and and_62 (and_62_out, and_61_out, d_ff_1_qn, C);
  D_Flip_Flop d_ff_34 (.D(d_ff_6_q), .clk(and_63_out), .Q(d_ff_34_q));  // open: Qn, preset, reset
  and and_63 (and_63_out, and_61_out, d_ff_1_qn, C);
  D_Flip_Flop d_ff_35 (.D(d_ff_7_q), .clk(and_64_out), .Q(d_ff_35_q));  // open: Qn, preset, reset
  and and_64 (and_64_out, and_61_out, d_ff_1_qn, C);
  D_Flip_Flop d_ff_36 (.D(d_ff_8_q), .clk(and_65_out), .Q(d_ff_36_q));  // open: Qn, preset, reset
  and and_65 (and_65_out, and_61_out, d_ff_1_qn, C);
  and and_66 (and_66_out, and_61_out, d_ff_1_q);
  and and_67 (and_67_out, d_ff_33_q, and_66_out);
  and and_68 (and_68_out, d_ff_34_q, and_66_out);
  and and_69 (and_69_out, d_ff_35_q, and_66_out);
  and and_70 (and_70_out, d_ff_36_q, and_66_out);
  not not_10 (not_10_out, d_ff_4_q);
  not not_11 (not_11_out, d_ff_3_q);
  not not_12 (not_12_out, d_ff_2_q);
  and and_71 (and_71_out, not_10_out, not_11_out, not_12_out);
  D_Flip_Flop d_ff_37 (.D(d_ff_5_q), .clk(and_72_out), .Q(d_ff_37_q));  // open: Qn, preset, reset
  and and_72 (and_72_out, and_71_out, d_ff_1_qn, C);
  D_Flip_Flop d_ff_38 (.D(d_ff_6_q), .clk(and_73_out), .Q(d_ff_38_q));  // open: Qn, preset, reset
  and and_73 (and_73_out, and_71_out, d_ff_1_qn, C);
  D_Flip_Flop d_ff_39 (.D(d_ff_7_q), .clk(and_74_out), .Q(d_ff_39_q));  // open: Qn, preset, reset
  and and_74 (and_74_out, and_71_out, d_ff_1_qn, C);
  D_Flip_Flop d_ff_40 (.D(d_ff_8_q), .clk(and_75_out), .Q(d_ff_40_q));  // open: Qn, preset, reset
  and and_75 (and_75_out, and_71_out, d_ff_1_qn, C);
  and and_76 (and_76_out, and_71_out, d_ff_1_q);
  and and_77 (and_77_out, d_ff_37_q, and_76_out);
  and and_78 (and_78_out, d_ff_38_q, and_76_out);
  and and_79 (and_79_out, d_ff_39_q, and_76_out);
  and and_80 (and_80_out, d_ff_40_q, and_76_out);
  or or_1 (or_1_out, and_77_out, and_67_out, and_57_out, and_47_out, and_37_out, and_27_out, and_17_out, and_7_out);
  or or_2 (or_2_out, and_78_out, and_68_out, and_58_out, and_48_out, and_38_out, and_28_out, and_18_out, and_8_out);
  or or_3 (or_3_out, and_79_out, and_69_out, and_59_out, and_49_out, and_39_out, and_29_out, and_19_out, and_9_out);
  or or_4 (or_4_out, and_80_out, and_70_out, and_60_out, and_50_out, and_40_out, and_30_out, and_20_out, and_10_out);
  and and_81 (and_81_out, d_ff_1_q, C);
  D_Flip_Flop d_ff_41 (.D(or_1_out), .clk(and_81_out), .Q(Output3));  // open: Qn, preset, reset
  D_Flip_Flop d_ff_42 (.D(or_2_out), .clk(and_81_out), .Q(Output2));  // open: Qn, preset, reset
  D_Flip_Flop d_ff_43 (.D(or_3_out), .clk(and_81_out), .Q(Output1));  // open: Qn, preset, reset
  D_Flip_Flop d_ff_44 (.D(or_4_out), .clk(and_81_out), .Q(Output0));  // open: Qn, preset, reset

  // Notes on the sheet:
  //   Address7
  //   Address7
  //   Address7
  //   Address7
  //   Address6
  //   Address6
  //   Address6
  //   Address6
  //   Address5
  //   Address5
  //   Address5
  //   Address5
  //   Address4
  //   Address4
  //   Address4
  //   Address4
  //   Address3
  //   Address3
  //   Address3
  //   Address3
  //   Address2
  //   Address2
  //   Address2
  //   Address2
  //   Address1
  //   Address1
  //   Address1
  //   Address1
  //   Address0
  //   Address0
  //   Address0
  //   Address0
endmodule

module Ram2Nibble (
  input  C,
  input  Mode,
  input  Address0,
  input  Input3,
  input  Input2,
  input  Input1,
  input  Input0,
  output Output3,
  output Output2,
  output Output1,
  output Output0
);

  wire and_1_out, and_2_out, and_3_out, and_4_out, and_5_out, and_6_out, and_7_out, and_8_out, and_9_out,
       and_10_out, and_11_out, and_12_out, and_13_out, and_14_out, and_15_out, and_16_out, and_17_out,
       and_18_out, and_19_out, d_ff_1_q, d_ff_1_qn, d_ff_2_q, d_ff_3_q, d_ff_4_q, d_ff_5_q, d_ff_6_q,
       d_ff_7_q, d_ff_8_q, d_ff_9_q, d_ff_10_q, d_ff_11_q, d_ff_12_q, d_ff_13_q, d_ff_14_q, not_1_out,
       or_1_out, or_2_out, or_3_out, or_4_out;

  D_Flip_Flop d_ff_1 (.D(Mode), .clk(C), .Q(d_ff_1_q), .Qn(d_ff_1_qn));  // open: preset, reset
  D_Flip_Flop d_ff_2 (.D(Address0), .clk(C), .Q(d_ff_2_q));  // open: Qn, preset, reset
  D_Flip_Flop d_ff_3 (.D(Input3), .clk(C), .Q(d_ff_3_q));  // open: Qn, preset, reset
  D_Flip_Flop d_ff_4 (.D(Input2), .clk(C), .Q(d_ff_4_q));  // open: Qn, preset, reset
  D_Flip_Flop d_ff_5 (.D(Input1), .clk(C), .Q(d_ff_5_q));  // open: Qn, preset, reset
  D_Flip_Flop d_ff_6 (.D(Input0), .clk(C), .Q(d_ff_6_q));  // open: Qn, preset, reset
  and and_1 (and_1_out, d_ff_2_q, d_ff_1_q);
  D_Flip_Flop d_ff_7 (.D(d_ff_3_q), .clk(and_2_out), .Q(d_ff_7_q));  // open: Qn, preset, reset
  and and_2 (and_2_out, d_ff_2_q, d_ff_1_qn, C);
  D_Flip_Flop d_ff_8 (.D(d_ff_4_q), .clk(and_3_out), .Q(d_ff_8_q));  // open: Qn, preset, reset
  and and_3 (and_3_out, d_ff_2_q, d_ff_1_qn, C);
  D_Flip_Flop d_ff_9 (.D(d_ff_5_q), .clk(and_4_out), .Q(d_ff_9_q));  // open: Qn, preset, reset
  and and_4 (and_4_out, d_ff_2_q, d_ff_1_qn, C);
  D_Flip_Flop d_ff_10 (.D(d_ff_6_q), .clk(and_5_out), .Q(d_ff_10_q));  // open: Qn, preset, reset
  and and_5 (and_5_out, d_ff_2_q, d_ff_1_qn, C);
  and and_6 (and_6_out, d_ff_7_q, and_1_out);
  and and_7 (and_7_out, d_ff_8_q, and_1_out);
  and and_8 (and_8_out, d_ff_9_q, and_1_out);
  and and_9 (and_9_out, d_ff_10_q, and_1_out);
  not not_1 (not_1_out, d_ff_2_q);
  and and_10 (and_10_out, not_1_out, d_ff_1_q);
  D_Flip_Flop d_ff_11 (.D(d_ff_3_q), .clk(and_11_out), .Q(d_ff_11_q));  // open: Qn, preset, reset
  and and_11 (and_11_out, not_1_out, d_ff_1_qn, C);
  D_Flip_Flop d_ff_12 (.D(d_ff_4_q), .clk(and_12_out), .Q(d_ff_12_q));  // open: Qn, preset, reset
  and and_12 (and_12_out, not_1_out, d_ff_1_qn, C);
  D_Flip_Flop d_ff_13 (.D(d_ff_5_q), .clk(and_13_out), .Q(d_ff_13_q));  // open: Qn, preset, reset
  and and_13 (and_13_out, not_1_out, d_ff_1_qn, C);
  D_Flip_Flop d_ff_14 (.D(d_ff_6_q), .clk(and_14_out), .Q(d_ff_14_q));  // open: Qn, preset, reset
  and and_14 (and_14_out, not_1_out, d_ff_1_qn, C);
  and and_15 (and_15_out, d_ff_11_q, and_10_out);
  and and_16 (and_16_out, d_ff_12_q, and_10_out);
  and and_17 (and_17_out, d_ff_13_q, and_10_out);
  and and_18 (and_18_out, d_ff_14_q, and_10_out);
  and and_19 (and_19_out, d_ff_1_q, C);
  or or_1 (or_1_out, and_15_out, and_6_out);
  or or_2 (or_2_out, and_16_out, and_7_out);
  or or_3 (or_3_out, and_17_out, and_8_out);
  or or_4 (or_4_out, and_18_out, and_9_out);
  D_Flip_Flop d_ff_15 (.D(or_1_out), .clk(and_19_out), .Q(Output3));  // open: Qn, preset, reset
  D_Flip_Flop d_ff_16 (.D(or_2_out), .clk(and_19_out), .Q(Output2));  // open: Qn, preset, reset
  D_Flip_Flop d_ff_17 (.D(or_3_out), .clk(and_19_out), .Q(Output1));  // open: Qn, preset, reset
  D_Flip_Flop d_ff_18 (.D(or_4_out), .clk(and_19_out), .Q(Output0));  // open: Qn, preset, reset

  // Notes on the sheet:
  //   Address1
  //   Address1
  //   Address1
  //   Address1
  //   Address0
  //   Address0
  //   Address0
  //   Address0
endmodule

module AddOne (
  input  _0,
  input  _1,
  input  _2,
  input  _3,
  input  in_5,
  input  in_6,
  input  in_7,
  input  in_8,
  input  in_9,
  input  in_10,
  input  in_11,
  input  in_12,
  input  in_13,
  input  in_14
);

  wire and_1_out, and_2_out, bitA, bitB, clock_1_out, clock_2_out, clock_3_out, clock_4_out, clock_5_out,
       decoder_1_out0, decoder_1_out1;
  wire [2:0] myalu_1_result0, register_1_q;
  wire [3:0] multiplexer_1_out, multiplexer_2_out, myalu_2_result0, ram2nibble_1_output3,
       ram8nibble_1_output3, register_3_q, register_4_q, register_5_q;
  wire [3:2] register_2_q;

  Register #(.width(3)) register_1 (.D(myalu_1_result0), .clk(clock_1_out), .Q(register_1_q));  // open: en, clr
  Clock clock_1 (.out(clock_1_out));
  Clock clock_2 (.out(clock_2_out));
  // Probe on myalu_1_result0[0]
  MyALU myalu_1 (
    .C(clock_2_out), .Operation1(in_6), .AInvert(in_7), .BInvert(in_8), .Operation0(in_9), .A0(in_10),
    .B0(register_1_q[0]), .A1(in_11), .B1(register_1_q[1]), .A2(in_12), .B2(register_1_q[2]), .A3(in_13),
    .B3(in_14), .Result0(myalu_1_result0[0]), .Result1(myalu_1_result0[1]), .Result2(myalu_1_result0[2]));  // open: Result3, Status0_Sign, Status1_Zero, Status2_SignOverflow
  // Probe on myalu_1_result0[1]
  // Probe on myalu_1_result0[2]
  Ram8Nibble ram8nibble_1 (
    .Mode(register_1_q[0]), .Address0(register_1_q[1]), .Address1(register_1_q[2]), .Address2(_0),
    .Input3(_1), .Input2(_2), .Input1(_3), .Input0(_3), .Output3(ram8nibble_1_output3[0]),
    .Output2(ram8nibble_1_output3[1]), .Output1(ram8nibble_1_output3[2]), .Output0(ram8nibble_1_output3[3]));  // open: C
  Register #(.width(4)) register_2 (
    .D(ram8nibble_1_output3), .clk(clock_3_out), .Q({register_2_q, bitB, bitA}));  // open: en, clr
  Clock clock_3 (.out(clock_3_out));
  Clock clock_4 (.out(clock_4_out));
  Decoder decoder_1 (.out0(decoder_1_out0), .out1(decoder_1_out1), .en(in_5));  // open: sel
  Register #(.width(4)) register_3 (.D(ram2nibble_1_output3), .clk(and_1_out), .Q(register_3_q));  // open: en, clr
  and and_1 (and_1_out, clock_4_out, decoder_1_out0);
  Register #(.width(4)) register_4 (.D(ram2nibble_1_output3), .clk(and_2_out), .Q(register_4_q));  // open: en, clr
  and and_2 (and_2_out, clock_4_out, decoder_1_out1);
  Multiplexer #(.width(4)) multiplexer_1 (
    .in0(register_3_q), .in1(register_4_q), .out(multiplexer_1_out), .sel(register_2_q[2]));
  Multiplexer #(.width(4)) multiplexer_2 (
    .in0(register_3_q), .in1(register_4_q), .out(multiplexer_2_out), .sel(register_2_q[3]));
  MyALU myalu_2 (
    .A0(multiplexer_1_out[0]), .B0(multiplexer_2_out[0]), .A1(multiplexer_1_out[1]),
    .B1(multiplexer_2_out[1]), .A2(multiplexer_1_out[2]), .B2(multiplexer_2_out[2]),
    .A3(multiplexer_1_out[3]), .B3(multiplexer_2_out[3]), .Result0(myalu_2_result0[0]),
    .Result1(myalu_2_result0[1]), .Result2(myalu_2_result0[2]), .Result3(myalu_2_result0[3]));  // open: C, Operation1, AInvert, BInvert, Operation0, Status0_Sign, Status1_Zero, Status2_SignOverflow
  Register #(.width(4)) register_5 (.D(myalu_2_result0), .clk(clock_5_out), .Q(register_5_q));  // open: en, clr
  Clock clock_5 (.out(clock_5_out));
  Ram2Nibble ram2nibble_1 (
    .Address0(register_5_q[0]), .Input3(register_5_q[1]), .Input2(register_5_q[2]), .Input1(register_5_q[3]),
    .Output3(ram2nibble_1_output3[0]), .Output2(ram2nibble_1_output3[1]), .Output1(ram2nibble_1_output3[2]),
    .Output0(ram2nibble_1_output3[3]));  // open: C, Mode, Input0

  // Notes on the sheet:
  //   CP
  //   Instruction RAM
  //   IR
  //   Write Select
  //   Write Data
  //   Read0
  //   Read1
  //   ALU Out
  //   Data RAM
endmodule

module CU (
  input  bitC,
  input  bitD,
  input  LOAD,
  input  SAVE,
  input  ADD,
  input  SUB,
  output BINV,
  output DATAA,
  output READB,
  output READA,
  output WSELE,
  output WENAB,
  output DATAW
);

  wire not_1_out;

  not not_1 (not_1_out, ADD);
  and and_1 (BINV, not_1_out, SUB);
  not not_2 (WENAB, SAVE);

  assign DATAA = bitD;
  assign DATAW = SAVE;
  assign READA = bitC;
  assign READB = bitD;
  assign WSELE = bitC;
endmodule

module MyALUComb (
  input  Operation1,
  input  AInvert,
  input  BInvert,
  input  Operation0,
  input  A0,
  input  B0,
  input  A1,
  input  B1,
  input  A2,
  input  B2,
  input  A3,
  input  B3,
  output Result0,
  output Result1,
  output Result2,
  output Result3,
  output Status0_Sign,
  output Status1_Zero,
  output Status2_SignOverflow
);

  wire and_1_out, and_2_out, and_3_out, and_4_out, and_5_out, and_6_out, and_7_out, and_8_out, and_9_out,
       and_10_out, and_11_out, and_12_out, and_13_out, and_14_out, and_15_out, and_16_out, and_17_out,
       and_18_out, and_19_out, and_20_out, and_21_out, and_22_out, and_23_out, and_24_out, and_25_out,
       and_26_out, and_27_out, and_28_out, and_29_out, and_30_out, and_31_out, and_32_out, and_33_out,
       and_34_out, and_35_out, and_36_out, and_37_out, and_38_out, and_39_out, and_40_out, and_41_out,
       and_42_out, and_43_out, and_44_out, and_45_out, and_46_out, and_47_out, and_48_out, and_49_out,
       and_50_out, and_51_out, and_52_out, and_53_out, and_54_out, not_1_out, not_2_out, not_3_out,
       not_4_out, not_5_out, not_6_out, not_7_out, not_8_out, not_9_out, not_10_out, not_11_out, not_12_out,
       not_13_out, not_14_out, not_15_out, not_16_out, not_17_out, not_18_out, not_19_out, not_20_out,
       not_21_out, not_22_out, or_1_out, or_2_out, or_3_out, or_4_out, or_5_out, or_6_out, or_7_out,
       or_8_out, or_9_out, or_10_out, or_11_out, or_13_out, or_14_out, or_15_out, or_16_out, or_17_out,
       or_18_out, or_19_out, or_20_out, xor_1_out, xor_2_out, xor_3_out, xor_4_out, xor_5_out, xor_6_out,
       xor_7_out, xor_8_out, xor_9_out;

  not not_1 (not_1_out, A0);
  not not_2 (not_2_out, B0);
  not not_3 (not_3_out, A1);
  not not_4 (not_4_out, B1);
  not not_5 (not_5_out, A2);
  not not_6 (not_6_out, B2);
  not not_7 (not_7_out, A3);
  not not_8 (not_8_out, B3);
  and and_1 (and_1_out, A0, not_9_out);
  not not_9 (not_9_out, AInvert);
  and and_2 (and_2_out, AInvert, not_1_out);
  and and_3 (and_3_out, B0, not_10_out);
  not not_10 (not_10_out, BInvert);
  and and_4 (and_4_out, BInvert, not_2_out);
  and and_5 (and_5_out, A1, not_11_out);
  not not_11 (not_11_out, AInvert);
  and and_6 (and_6_out, AInvert, not_3_out);
  and and_7 (and_7_out, B1, not_12_out);
  not not_12 (not_12_out, BInvert);
  and and_8 (and_8_out, BInvert, not_4_out);
  and and_9 (and_9_out, A2, not_13_out);
  not not_13 (not_13_out, AInvert);
  and and_10 (and_10_out, AInvert, not_5_out);
  and and_11 (and_11_out, B2, not_14_out);
  not not_14 (not_14_out, BInvert);
  and and_12 (and_12_out, BInvert, not_6_out);
  and and_13 (and_13_out, A3, not_15_out);
  not not_15 (not_15_out, AInvert);
  and and_14 (and_14_out, AInvert, not_7_out);
  and and_15 (and_15_out, B3, not_16_out);
  not not_16 (not_16_out, BInvert);
  and and_16 (and_16_out, BInvert, not_8_out);
  or or_1 (or_1_out, and_1_out, and_2_out);
  or or_2 (or_2_out, and_3_out, and_4_out);
  or or_3 (or_3_out, and_5_out, and_6_out);
  or or_4 (or_4_out, and_7_out, and_8_out);
  or or_5 (or_5_out, and_9_out, and_10_out);
  or or_6 (or_6_out, and_11_out, and_12_out);
  or or_7 (or_7_out, and_13_out, and_14_out);
  or or_8 (or_8_out, and_15_out, and_16_out);
  xor xor_1 (xor_1_out, or_1_out, or_2_out);
  and and_17 (and_17_out, or_2_out, or_1_out);
  xor xor_2 (xor_2_out, or_3_out, or_4_out);
  and and_18 (and_18_out, or_4_out, or_3_out);
  xor xor_3 (xor_3_out, or_5_out, or_6_out);
  and and_19 (and_19_out, or_6_out, or_5_out);
  xor xor_4 (xor_4_out, or_7_out, or_8_out);
  and and_20 (and_20_out, or_8_out, or_7_out);
  xor xor_5 (xor_5_out, BInvert, xor_1_out);
  and and_21 (and_21_out, xor_1_out, BInvert);
  xor xor_6 (xor_6_out, or_9_out, xor_2_out);
  and and_22 (and_22_out, xor_2_out, or_9_out);
  xor xor_7 (xor_7_out, or_10_out, xor_3_out);
  and and_23 (and_23_out, xor_3_out, or_10_out);
  xor xor_8 (xor_8_out, or_11_out, xor_4_out);
  and and_24 (and_24_out, xor_4_out, or_11_out);
  or or_9 (or_9_out, and_21_out, and_17_out);
  or or_10 (or_10_out, and_22_out, and_18_out);
  or or_11 (or_11_out, and_23_out, and_19_out);
  // OR_Gate or_12 has open pins: in0=and_24_out, in1=and_20_out, out=open
  not not_17 (not_17_out, Operation1);
  or or_13 (or_13_out, or_1_out, or_2_out);
  and and_25 (and_25_out, or_1_out, or_2_out);
  or or_14 (or_14_out, or_3_out, or_4_out);
  and and_26 (and_26_out, or_3_out, or_4_out);
  or or_15 (or_15_out, or_5_out, or_6_out);
  and and_27 (and_27_out, or_5_out, or_6_out);
  or or_16 (or_16_out, or_7_out, or_8_out);
  and and_28 (and_28_out, or_7_out, or_8_out);
  not not_18 (not_18_out, Operation0);
  and and_29 (and_29_out, xor_5_out, Operation1);
  and and_30 (and_30_out, or_13_out, not_17_out);
  and and_31 (and_31_out, and_25_out, not_17_out);
  and and_32 (and_32_out, xor_6_out, Operation1);
  and and_33 (and_33_out, or_14_out, not_17_out);
  and and_34 (and_34_out, and_26_out, not_17_out);
  and and_35 (and_35_out, xor_7_out, Operation1);
  and and_36 (and_36_out, or_15_out, not_17_out);
  and and_37 (and_37_out, and_27_out, not_17_out);
  and and_38 (and_38_out, xor_8_out, Operation1);
  and and_39 (and_39_out, or_16_out, not_17_out);
  and and_40 (and_40_out, and_28_out, not_17_out);
  and and_41 (and_41_out, and_29_out, not_18_out);
  and and_42 (and_42_out, Operation0, and_30_out);
  and and_43 (and_43_out, not_18_out, and_31_out);
  and and_44 (and_44_out, and_32_out, not_18_out);
  and and_45 (and_45_out, Operation0, and_33_out);
  and and_46 (and_46_out, not_18_out, and_34_out);
  and and_47 (and_47_out, and_35_out, not_18_out);
  and and_48 (and_48_out, Operation0, and_36_out);
  and and_49 (and_49_out, not_18_out, and_37_out);
  and and_50 (and_50_out, and_38_out, not_18_out);
  and and_51 (and_51_out, Operation0, and_39_out);
  and and_52 (and_52_out, not_18_out, and_40_out);
  or or_17 (or_17_out, and_41_out, and_42_out);
  or or_18 (or_18_out, and_44_out, and_45_out);
  or or_19 (or_19_out, and_47_out, and_48_out);
  or or_20 (or_20_out, and_50_out, and_51_out);
  or or_21 (Result0, or_17_out, and_43_out);
  or or_22 (Result1, or_18_out, and_46_out);
  or or_23 (Result2, or_19_out, and_49_out);
  or or_24 (Result3, or_20_out, and_52_out);
  xor xor_9 (xor_9_out, or_7_out, or_8_out);
  and and_53 (and_53_out, or_7_out, or_8_out);
  and and_54 (and_54_out, Result3, xor_9_out);
  not not_19 (not_19_out, Result0);
  not not_20 (not_20_out, Result1);
  not not_21 (not_21_out, Result2);
  not not_22 (not_22_out, Result3);
  or or_25 (Status0_Sign, and_54_out, and_53_out);
  and and_55 (Status1_Zero, not_19_out, not_20_out, not_21_out, not_22_out);
  xor xor_10 (Status2_SignOverflow, Result3, Status0_Sign);

  // Notes on the sheet:
  //   A0: initial=0x1
  //   B0: initial=0x1
  //   Multiplexor for inverting
  //    Full bit adder circuit
  //   Multiplexer to choose operation
endmodule
